// Logisim project ALU.circ as structural Verilog: 3 circuits, main circuit ALU
module ALU (
  input  [15:0] Data_In1,
  input  [15:0] Data_In2,
  input  [7:0] Control,
  output [15:0] Data_Out,
  output Negative,
  output Zero,
  output Carry_Out,
  output Overflow
);

  wire adder_1_carry_out, adder_1_overflow, and_2_out, clock_1_out, clock_2_out, clock_3_out, clock_4_out,
       multiplexer_2_out, multiplexer_3_out, subtractor_1_carry_out, subtractor_1_overflow;
  wire [15:0] adder_1_output, and_1_out, negator_1_out, not_1_out, not_2_out, or_1_out, shifter_1_out,
       shifter_2_out, shifter_3_out, shifter_4_out, subtractor_1_output, xor_1_out;

  Adder adder_1 (
    .Input1(Data_In1), .Input2(Data_In2), .Output(adder_1_output), .Carry_Out(adder_1_carry_out),
    .Overflow(adder_1_overflow));
  Subtractor subtractor_1 (
    .Input1(Data_In1), .Input2(Data_In2), .Output(subtractor_1_output), .Carry_Out(subtractor_1_carry_out),
    .Overflow(subtractor_1_overflow));
  assign and_1_out = Data_In1 & Data_In2;  // AND_Gate and_1, 16 bits wide
  assign or_1_out = Data_In1 | Data_In2;  // OR_Gate or_1, 16 bits wide
  assign xor_1_out = Data_In1 ^ Data_In2;  // XOR_Gate xor_1, 16 bits wide
  Shifter #(.width(16)) shifter_1 (.in(Data_In1), .\dist (Data_In2[3:0]), .out(shifter_1_out));
  Shifter #(.width(16), .shift("lr")) shifter_2 (.in(Data_In1), .\dist (Data_In2[3:0]), .out(shifter_2_out));
  Shifter #(.width(16), .shift("ar")) shifter_3 (.in(Data_In1), .\dist (Data_In2[3:0]), .out(shifter_3_out));
  Shifter #(.width(16), .shift("rl")) shifter_4 (.in(Data_In1), .\dist (Data_In2[3:0]), .out(shifter_4_out));
  Negator #(.width(16)) negator_1 (.in(Data_In1), .out(negator_1_out));
  assign not_1_out = ~Data_In1;  // NOT_Gate not_1, 16 bits wide
  Multiplexer #(.select(4), .width(16), .disabled(0), .enable("false")) multiplexer_1 (
    .in0(and_1_out), .in1(or_1_out), .in2(xor_1_out), .in3(shifter_1_out), .in4(shifter_2_out),
    .in5(shifter_3_out), .in6(shifter_4_out), .in7(adder_1_output), .in8(subtractor_1_output),
    .in9(negator_1_out), .in10(not_1_out), .in14(Data_In1), .in15(Data_In2), .out(Data_Out),
    .sel(Control[3:0]));  // open: in11, in12, in13
  Multiplexer #(.select(4), .disabled(0), .enable("false")) multiplexer_2 (
    .in7(adder_1_carry_out), .in8(subtractor_1_carry_out), .out(multiplexer_2_out), .sel(Control[3:0]));  // open: in0, in1, in2, in3, in4, in5, in6, in9, in10, in11, in12, in13, in14, in15
  Multiplexer #(.select(4), .disabled(0), .enable("false")) multiplexer_3 (
    .in7(adder_1_overflow), .in8(subtractor_1_overflow), .out(multiplexer_3_out), .sel(Control[3:0]));  // open: in0, in1, in2, in3, in4, in5, in6, in9, in10, in11, in12, in13, in14, in15
  assign not_2_out = ~Data_Out;  // NOT_Gate not_2, 16 bits wide
  and and_2 (and_2_out, not_2_out[0], not_2_out[1], not_2_out[2], not_2_out[3], not_2_out[4], not_2_out[5], not_2_out[6], not_2_out[7], not_2_out[8], not_2_out[9], not_2_out[10], not_2_out[11], not_2_out[12], not_2_out[13], not_2_out[14], not_2_out[15]);
  Register #(.width(1), .trigger("falling")) register_1 (
    .D(Data_Out[15]), .en(Control[7]), .Q(Negative), .clk(clock_1_out));  // open: clr
  Clock clock_1 (.out(clock_1_out));
  Register #(.width(1), .trigger("falling")) register_2 (
    .D(and_2_out), .en(Control[6]), .Q(Zero), .clk(clock_2_out));  // open: clr
  Clock clock_2 (.out(clock_2_out));
  Register #(.width(1), .trigger("falling")) register_3 (
    .D(multiplexer_2_out), .en(Control[5]), .Q(Carry_Out), .clk(clock_3_out));  // open: clr
  Clock clock_3 (.out(clock_3_out));
  Register #(.width(1), .trigger("falling")) register_4 (
    .D(multiplexer_3_out), .en(Control[4]), .Q(Overflow), .clk(clock_4_out));  // open: clr
  Clock clock_4 (.out(clock_4_out));
endmodule

module Adder (
  input  [15:0] Input1,
  input  [15:0] Input2,
  output [15:0] Output,
  output Carry_Out,
  output Overflow
);

  wire adder_1_cout;

  Adder_part #(.width(15)) adder_1 (
    .a(Input1[14:0]), .b(Input2[14:0]), .out(Output[14:0]), .cin(1'b0), .cout(adder_1_cout));
  Adder_part #(.width(1)) adder_2 (
    .a(Input1[15]), .b(Input2[15]), .out(Output[15]), .cin(adder_1_cout), .cout(Carry_Out));
  xor xor_1 (Overflow, Carry_Out, adder_1_cout);

  // Notes on the sheet:
  //   Output: pull=down
endmodule

module Subtractor (
  input  [15:0] Input1,
  input  [15:0] Input2,
  output [15:0] Output,
  output Carry_Out,
  output Overflow
);

  wire adder_1_cout, not_2_out;
  wire [14:0] not_1_out;

  assign not_1_out = ~Input2[14:0];  // NOT_Gate not_1, 15 bits wide
  not not_2 (not_2_out, Input2[15]);
  Adder_part #(.width(15)) adder_1 (
    .a(Input1[14:0]), .b(not_1_out), .out(Output[14:0]), .cin(1'b1), .cout(adder_1_cout));
  Adder_part #(.width(1)) adder_2 (
    .a(Input1[15]), .b(not_2_out), .out(Output[15]), .cin(adder_1_cout), .cout(Carry_Out));
  xor xor_1 (Overflow, Carry_Out, adder_1_cout);

  // Notes on the sheet:
  //   Output: pull=down
endmodule
