// Logisim project processor.circ as structural Verilog: 2 circuits, main circuit main
module main (
  input  [15:0] Processor_Data_In,
  input  in_2,
  output out_3,
  output [1:0] out_4,
  output [1:0] out_5,
  output [2:0] out_6,
  output out_7,
  output [15:0] Processor_Data_Out,
  output out_9,
  output [7:0] out_10,
  output out_11,
  output [15:0] out_12,
  output [2:0] out_13,
  output out_14,
  output [2:0] out_15,
  output out_16,
  output [3:0] out_17,
  output out_18,
  output [2:0] out_19,
  output [15:0] out_20,
  output [2:0] out_21,
  output [15:0] out_22,
  output [2:0] out_23,
  output out_24,
  output [7:0] out_25,
  output [15:0] out_26
);

  wire Add_ADD, Add_OP, Add_SUB, ALU_CMP, ALU_Common, ALU_OP, ALU_Source2, ALU_TST, and_1_out, and_2_out,
       and_3_out, and_4_out, and_10_out, Branch_Subroutine_OP, Branch_Taken, BranchISR, buffer_1_out,
       buffer_2_out, buffer_3_out, C, clock_1_out, clock_2_out, clock_3_out, clock_4_out, clock_5_out,
       clock_6_out, clock_7_out, clock_8_out, clock_9_out, clock_10_out, clock_11_out, clock_12_out,
       clock_13_out, clock_14_out, clock_15_out, clock_16_out, clock_17_out, clock_18_out, clock_19_out,
       clock_20_out, clock_21_out, clock_22_out, clock_23_out, clock_24_out, clock_25_out, clock_26_out,
       clock_27_out, clock_28_out, clock_29_out, clock_30_out, clock_31_out, clock_32_out, clock_33_out,
       clock_34_out, clock_35_out, clock_36_out, clock_37_out, comparator_1_eq, comparator_2_eq,
       comparator_3_eq, comparator_4_eq, comparator_5_eq, comparator_6_eq, comparator_7_eq, comparator_8_eq,
       comparator_9_eq, Cond_Branch_OP, controlled_buffer_218_out, decoder_3_out0, decoder_3_out7,
       decoder_5_out0, decoder_8_out0, decoder_8_out1, decoder_8_out2, decoder_8_out3, decoder_8_out4,
       decoder_8_out5, decoder_8_out6, decoder_8_out7, decoder_8_out8, decoder_8_out9, decoder_8_out10,
       decoder_11_out0, decoder_11_out1, decoder_11_out2, decoder_11_out3, decoder_11_out4, decoder_11_out5,
       decoder_11_out6, decoder_11_out7, demultiplexer_1_out0, demultiplexer_1_out2, FlushD, FlushDWillCome,
       FlushE, Inherent_IOF, Inherent_ION, Inherent_NOP, Inherent_OP, Inherent_RTI, Inherent_RTS,
       LD_ST_Imm_LD, LD_ST_Imm_OP, LD_ST_Imm_STR, LD_ST_Reg_LD, LD_ST_Reg_OP, Mem_to_Reg, Mem_Write,
       MemToRegE, Move_Imm_ADD, Move_Imm_CMP, Move_Imm_MOV, Move_Imm_OP, Move_Imm_SUB, Move_Long_OP, N,
       nor_1_out, not_1_out, not_2_out, not_3_out, not_4_out, not_5_out, not_6_out, not_7_out, not_8_out,
       not_9_out, not_10_out, not_11_out, not_12_out, or_1_out, or_2_out, or_4_out, or_5_out, PC_Source,
       register_5_q, register_15_q, register_27_q, register_28_q, register_29_q, RegWriteE, RegWriteM, RTI,
       Shift_OP, StallD, Uncond_Branch_OP, V, xnor_1_out, xor_1_out, xor_2_out, Z;
  wire [1:0] and_6_out, and_8_out, controlled_buffer_113_out, IO_Selection;
  wire [2:0] adder_2_out, multiplexer_13_out, multiplexer_14_out, RegReadAdr1E, RegReadAdr2E, RegWriteAdrE,
       RegWriteAdrM, Stack_Pointer_q, subtractor_2_out, subtractor_3_out;
  wire [3:0] multiplexer_18_out;
  wire [6:0] keyboard_1_data;
  wire [7:0] multiplexer_6_out, multiplexer_9_out;
  wire [8:8] keyboard_1_avail;
  wire [11:0] adder_1_out, ISRAdr, multiplexer_1_out, multiplexer_2_out, PC, r0_q, r1_q, r2_q, r3_q, r4_q,
       r5_q, r6_q, r7_q, RetrunAdr_q, RTSAdr, subtractor_1_out;
  wire [11:11] multiplexer_15_out, multiplexer_16_out;
  wire [15:0] ALUOutM, IO_Data_In, IO_Data_Out, IR, multiplexer_3_out, multiplexer_4_out, multiplexer_5_out,
       OffsetRegisterE, ram_1_data, register_11_q, register_12_q, register_22_q, register_23_q,
       register_24_q, register_file_1_data_out1, register_file_1_data_out2, rom_1_data;

  Multiplexer #(.width(12), .disabled(0), .enable("false")) multiplexer_1 (
    .in0(adder_1_out), .in1(ISRAdr), .out(multiplexer_1_out), .sel(BranchISR));
  Pull_Resistor pull_resistor_1 (.node(BranchISR));
  Hex_Digit_Display hex_digit_display_1 (.value(out_26[15:12]));  // open: dp
  assign out_13 = Inherent_RTS ? 3'b000 : 3'bz;  // Controlled_Buffer controlled_buffer_1
  Register #(.width(12)) u_PC (.D(multiplexer_1_out), .en(not_1_out), .Q(PC), .clk(clock_1_out));  // open: clr
  Clock clock_1 (.out(clock_1_out));
  not not_1 (not_1_out, StallD);
  Multiplexer #(.width(12), .disabled(0), .enable("false")) multiplexer_2 (
    .in0(12'h1), .in1(out_12[11:0]), .out(multiplexer_2_out), .sel(PC_Source));
  Hex_Digit_Display hex_digit_display_2 (.value(out_26[11:8]));  // open: dp
  Hex_Digit_Display hex_digit_display_3 (.value(out_26[7:4]));  // open: dp
  assign out_13 = Inherent_NOP ? 3'b000 : 3'bz;  // Controlled_Buffer controlled_buffer_2
  assign out_15 = Inherent_NOP ? 3'b000 : 3'bz;  // Controlled_Buffer controlled_buffer_3
  assign out_13 = Inherent_ION ? 3'b000 : 3'bz;  // Controlled_Buffer controlled_buffer_4
  assign out_15 = Inherent_ION ? 3'b000 : 3'bz;  // Controlled_Buffer controlled_buffer_5
  assign out_13 = Inherent_IOF ? 3'b000 : 3'bz;  // Controlled_Buffer controlled_buffer_6
  assign out_15 = Inherent_IOF ? 3'b000 : 3'bz;  // Controlled_Buffer controlled_buffer_7
  assign out_13 = Inherent_RTI ? 3'b000 : 3'bz;  // Controlled_Buffer controlled_buffer_8
  assign out_15 = Inherent_RTI ? 3'b000 : 3'bz;  // Controlled_Buffer controlled_buffer_9
  assign out_15 = Inherent_RTS ? 3'b000 : 3'bz;  // Controlled_Buffer controlled_buffer_10
  Adder #(.width(12)) adder_1 (.a(PC), .b(multiplexer_2_out), .out(adder_1_out));  // open: cin, cout
  Hex_Digit_Display hex_digit_display_4 (.value(out_26[3:0]));  // open: dp
  Subtractor #(.width(12)) subtractor_1 (.a(RTSAdr), .b(PC), .out(subtractor_1_out));  // open: bin, bout
  ROM #(.addrWidth(12), .dataWidth(16)) rom_1 (.addr(PC), .data(rom_1_data));  // open: sel
  assign out_11 = Inherent_NOP ? 1'b0 : 1'bz;  // Controlled_Buffer controlled_buffer_11
  assign out_12 = Inherent_NOP ? {16{1'b0}} : 16'bz;  // Controlled_Buffer controlled_buffer_12
  assign out_11 = Inherent_ION ? 1'b0 : 1'bz;  // Controlled_Buffer controlled_buffer_13
  assign out_12 = Inherent_ION ? {16{1'b0}} : 16'bz;  // Controlled_Buffer controlled_buffer_14
  assign out_11 = Inherent_IOF ? 1'b0 : 1'bz;  // Controlled_Buffer controlled_buffer_15
  assign out_12 = Inherent_IOF ? {16{1'b0}} : 16'bz;  // Controlled_Buffer controlled_buffer_16
  assign out_11 = Inherent_RTI ? 1'b0 : 1'bz;  // Controlled_Buffer controlled_buffer_17
  assign out_12 = Inherent_RTI ? {16{1'b0}} : 16'bz;  // Controlled_Buffer controlled_buffer_18
  assign out_11 = Inherent_RTS ? 1'b1 : 1'bz;  // Controlled_Buffer controlled_buffer_19
  assign out_12 = Inherent_RTS ? {4'b0000, subtractor_1_out} : 16'bz;  // Controlled_Buffer controlled_buffer_20
  not not_2 (not_2_out, StallD);
  Register #(.width(16)) register_1 (.D(rom_1_data), .en(not_2_out), .Q(IR), .clk(clock_2_out), .clr(FlushD));
  Clock clock_2 (.out(clock_2_out));
  Decoder #(.select(3), .disabled(0)) decoder_1 (
    .out0(Inherent_NOP), .out1(Inherent_ION), .out2(Inherent_IOF), .out3(Inherent_RTI), .out4(Inherent_RTS),
    .sel(IR[2:0]), .en(Inherent_OP));  // open: out5, out6, out7
  assign out_9 = Inherent_NOP ? 1'b0 : 1'bz;  // Controlled_Buffer controlled_buffer_21
  assign out_10 = Inherent_NOP ? {8{1'b0}} : 8'bz;  // Controlled_Buffer controlled_buffer_22
  assign out_9 = Inherent_ION ? 1'b0 : 1'bz;  // Controlled_Buffer controlled_buffer_23
  assign out_10 = Inherent_ION ? {8{1'b0}} : 8'bz;  // Controlled_Buffer controlled_buffer_24
  assign out_9 = Inherent_IOF ? 1'b0 : 1'bz;  // Controlled_Buffer controlled_buffer_25
  assign out_10 = Inherent_IOF ? {8{1'b0}} : 8'bz;  // Controlled_Buffer controlled_buffer_26
  assign out_9 = Inherent_RTI ? 1'b0 : 1'bz;  // Controlled_Buffer controlled_buffer_27
  assign out_10 = Inherent_RTI ? {8{1'b0}} : 8'bz;  // Controlled_Buffer controlled_buffer_28
  assign out_9 = Inherent_RTS ? 1'b0 : 1'bz;  // Controlled_Buffer controlled_buffer_29
  assign out_10 = Inherent_RTS ? 8'hf : 8'bz;  // Controlled_Buffer controlled_buffer_30
  assign out_7 = Inherent_NOP ? 1'b0 : 1'bz;  // Controlled_Buffer controlled_buffer_31
  assign out_6 = Inherent_NOP ? 3'b000 : 3'bz;  // Controlled_Buffer controlled_buffer_32
  assign out_3 = Inherent_NOP ? 1'b0 : 1'bz;  // Controlled_Buffer controlled_buffer_33
  assign out_7 = Inherent_ION ? 1'b0 : 1'bz;  // Controlled_Buffer controlled_buffer_34
  assign out_6 = Inherent_ION ? 3'b000 : 3'bz;  // Controlled_Buffer controlled_buffer_35
  assign out_3 = Inherent_ION ? 1'b0 : 1'bz;  // Controlled_Buffer controlled_buffer_36
  assign out_7 = Inherent_IOF ? 1'b0 : 1'bz;  // Controlled_Buffer controlled_buffer_37
  assign out_6 = Inherent_IOF ? 3'b000 : 3'bz;  // Controlled_Buffer controlled_buffer_38
  assign out_3 = Inherent_IOF ? 1'b0 : 1'bz;  // Controlled_Buffer controlled_buffer_39
  assign out_7 = Inherent_RTI ? 1'b0 : 1'bz;  // Controlled_Buffer controlled_buffer_40
  assign out_6 = Inherent_RTI ? 3'b000 : 3'bz;  // Controlled_Buffer controlled_buffer_41
  assign out_3 = Inherent_RTI ? 1'b0 : 1'bz;  // Controlled_Buffer controlled_buffer_42
  assign out_7 = Inherent_RTS ? 1'b0 : 1'bz;  // Controlled_Buffer controlled_buffer_43
  assign out_6 = Inherent_RTS ? 3'b000 : 3'bz;  // Controlled_Buffer controlled_buffer_44
  assign out_3 = Inherent_RTS ? 1'b0 : 1'bz;  // Controlled_Buffer controlled_buffer_45
  Clock clock_3 (.out(clock_3_out));
  Clock clock_4 (.out(clock_4_out));
  Clock clock_5 (.out(clock_5_out));
  Clock clock_6 (.out(clock_6_out));
  Clock clock_7 (.out(clock_7_out));
  Clock clock_8 (.out(clock_8_out));
  Clock clock_9 (.out(clock_9_out));
  Clock clock_10 (.out(clock_10_out));
  Clock clock_11 (.out(clock_11_out));
  Register_File register_file_1 (
    .Data_in(out_22), .Read_Write(out_24), .Data_out1(register_file_1_data_out1),
    .Data_out2(register_file_1_data_out2), .Data_Adr(out_23), .Adr1(out_13), .Adr2(out_15));
  Clock clock_12 (.out(clock_12_out));
  Clock clock_13 (.out(clock_13_out));
  assign out_16 = Inherent_NOP ? 1'b0 : 1'bz;  // Controlled_Buffer controlled_buffer_46
  assign out_17 = Inherent_NOP ? 4'b0000 : 4'bz;  // Controlled_Buffer controlled_buffer_47
  assign out_16 = Inherent_ION ? 1'b0 : 1'bz;  // Controlled_Buffer controlled_buffer_48
  assign out_17 = Inherent_ION ? 4'b0000 : 4'bz;  // Controlled_Buffer controlled_buffer_49
  assign out_16 = Inherent_IOF ? 1'b0 : 1'bz;  // Controlled_Buffer controlled_buffer_50
  assign out_17 = Inherent_IOF ? 4'b0000 : 4'bz;  // Controlled_Buffer controlled_buffer_51
  assign out_16 = Inherent_RTI ? 1'b0 : 1'bz;  // Controlled_Buffer controlled_buffer_52
  assign out_17 = Inherent_RTI ? 4'b0000 : 4'bz;  // Controlled_Buffer controlled_buffer_53
  assign out_16 = Inherent_RTS ? 1'b1 : 1'bz;  // Controlled_Buffer controlled_buffer_54
  assign out_17 = Inherent_RTS ? 4'b1111 : 4'bz;  // Controlled_Buffer controlled_buffer_55
  Register #(.width(1)) register_2 (.D(out_3), .Q(RegWriteE), .clk(clock_3_out), .clr(FlushE));  // open: en
  Register #(.width(3)) register_3 (.D(out_6), .Q(RegWriteAdrE), .clk(clock_4_out), .clr(FlushE));  // open: en
  Register #(.width(1)) register_4 (.D(out_7), .Q(MemToRegE), .clk(clock_5_out), .clr(FlushE));  // open: en
  Register #(.width(1)) register_5 (.D(out_9), .Q(register_5_q), .clk(clock_6_out), .clr(FlushE));  // open: en
  Register register_6 (.D(out_10), .Q(out_25), .clk(clock_7_out), .clr(FlushE));  // open: en
  Register #(.width(1)) register_7 (.D(out_11), .Q(ALU_Source2), .clk(clock_8_out), .clr(FlushE));  // open: en
  Register #(.width(16)) register_8 (.D(out_12), .Q(OffsetRegisterE), .clk(clock_9_out), .clr(FlushE));  // open: en
  Register #(.width(3)) register_9 (.D(out_13), .Q(RegReadAdr1E), .clk(clock_10_out), .clr(FlushE));  // open: en
  Register #(.width(3)) register_10 (.D(out_15), .Q(RegReadAdr2E), .clk(clock_11_out), .clr(FlushE));  // open: en
  Register #(.width(16)) register_11 (
    .D(register_file_1_data_out1), .Q(register_11_q), .clk(clock_12_out), .clr(FlushE));  // open: en
  Register #(.width(16)) register_12 (
    .D(register_file_1_data_out2), .Q(register_12_q), .clk(clock_13_out), .clr(FlushE));  // open: en
  assign out_14 = Inherent_ION ? 1'b1 : 1'bz;  // Controlled_Buffer controlled_buffer_56
  assign out_14 = Inherent_IOF ? 1'b0 : 1'bz;  // Controlled_Buffer controlled_buffer_57
  assign RTI = Inherent_RTI ? 1'b1 : 1'bz;  // Controlled_Buffer controlled_buffer_58
  assign out_14 = Inherent_RTI ? 1'b1 : 1'bz;  // Controlled_Buffer controlled_buffer_59
  Multiplexer #(.select(2), .width(16), .disabled(0), .enable("false")) multiplexer_3 (
    .in0(register_12_q), .in1(ALUOutM), .in2(out_22), .out(multiplexer_3_out), .sel(out_4));  // open: in3
  Multiplexer #(.select(2), .width(16), .disabled(0), .enable("false")) multiplexer_4 (
    .in0(register_11_q), .in1(ALUOutM), .in2(out_22), .out(multiplexer_4_out), .sel(out_5));  // open: in3
  Multiplexer #(.width(16), .disabled(0), .enable("false")) multiplexer_5 (
    .in0(multiplexer_3_out), .in1(OffsetRegisterE), .out(multiplexer_5_out), .sel(ALU_Source2));
  assign out_13 = Add_ADD ? IR[5:3] : 3'bz;  // Controlled_Buffer controlled_buffer_60
  assign out_15 = Add_ADD ? 3'b000 : 3'bz;  // Controlled_Buffer controlled_buffer_61
  assign out_13 = Add_SUB ? IR[5:3] : 3'bz;  // Controlled_Buffer controlled_buffer_62
  assign out_15 = Add_SUB ? 3'b000 : 3'bz;  // Controlled_Buffer controlled_buffer_63
  assign out_13 = Shift_OP ? IR[5:3] : 3'bz;  // Controlled_Buffer controlled_buffer_64
  assign out_15 = Shift_OP ? 3'b000 : 3'bz;  // Controlled_Buffer controlled_buffer_65
  ALU alu_1 (
    .Data_In1(multiplexer_4_out), .Data_In2(multiplexer_5_out), .Data_Out(out_20), .Negative(N), .Zero(Z),
    .Carry_Out(C), .Overflow(V), .Control(out_25));
  Register #(.width(1)) register_13 (.D(RegWriteE), .Q(RegWriteM), .clk(clock_14_out));  // open: en, clr
  Clock clock_14 (.out(clock_14_out));
  Register #(.width(3)) register_14 (.D(RegWriteAdrE), .Q(RegWriteAdrM), .clk(clock_15_out));  // open: en, clr
  Clock clock_15 (.out(clock_15_out));
  Register #(.width(1)) register_15 (.D(MemToRegE), .Q(register_15_q), .clk(clock_16_out));  // open: en, clr
  Clock clock_16 (.out(clock_16_out));
  Register #(.width(1)) register_16 (.D(register_5_q), .Q(Mem_Write), .clk(clock_17_out));  // open: en, clr
  Clock clock_17 (.out(clock_17_out));
  Register #(.width(16)) register_17 (.D(out_20), .Q(ALUOutM), .clk(clock_18_out));  // open: en, clr
  Clock clock_18 (.out(clock_18_out));
  Register #(.width(16)) register_18 (.D(multiplexer_3_out), .Q(IO_Data_In), .clk(clock_19_out));  // open: en, clr
  Clock clock_19 (.out(clock_19_out));
  assign out_11 = Add_ADD ? 1'b1 : 1'bz;  // Controlled_Buffer controlled_buffer_66
  assign out_12 = Add_ADD ? {{10{1'b0}}, IR[11:6]} : 16'bz;  // Controlled_Buffer controlled_buffer_67
  assign out_11 = Add_SUB ? 1'b1 : 1'bz;  // Controlled_Buffer controlled_buffer_68
  assign out_12 = Add_SUB ? {{10{1'b0}}, IR[11:6]} : 16'bz;  // Controlled_Buffer controlled_buffer_69
  assign out_11 = Shift_OP ? 1'b1 : 1'bz;  // Controlled_Buffer controlled_buffer_70
  assign out_12 = Shift_OP ? {{12{1'b0}}, IR[9:6]} : 16'bz;  // Controlled_Buffer controlled_buffer_71
  Multiplexer #(.select(2), .width(8), .enable("false")) multiplexer_6 (
    .in0(8'he3), .in1(8'he4), .in2(8'he5), .in3(8'he6), .out(multiplexer_6_out), .sel(IR[11:10]));
  Decoder #(.disabled(0)) decoder_2 (.out0(Add_ADD), .out1(Add_SUB), .sel(IR[12]), .en(Add_OP));
  assign out_9 = Add_ADD ? 1'b0 : 1'bz;  // Controlled_Buffer controlled_buffer_72
  assign out_10 = Add_ADD ? 8'hf7 : 8'bz;  // Controlled_Buffer controlled_buffer_73
  assign out_9 = Add_SUB ? 1'b0 : 1'bz;  // Controlled_Buffer controlled_buffer_74
  assign out_10 = Add_SUB ? 8'hf8 : 8'bz;  // Controlled_Buffer controlled_buffer_75
  assign out_10 = Shift_OP ? multiplexer_6_out : 8'bz;  // Controlled_Buffer controlled_buffer_76
  assign out_9 = Shift_OP ? 1'b0 : 1'bz;  // Controlled_Buffer controlled_buffer_77
  Clock clock_20 (.out(clock_20_out));
  Clock clock_21 (.out(clock_21_out));
  Clock clock_22 (.out(clock_22_out));
  Clock clock_23 (.out(clock_23_out));
  assign out_6 = Add_ADD ? IR[2:0] : 3'bz;  // Controlled_Buffer controlled_buffer_78
  assign out_6 = Add_SUB ? IR[2:0] : 3'bz;  // Controlled_Buffer controlled_buffer_79
  assign out_6 = Shift_OP ? IR[2:0] : 3'bz;  // Controlled_Buffer controlled_buffer_80
  Register #(.width(1)) register_19 (.D(RegWriteM), .Q(out_24), .clk(clock_20_out));  // open: en, clr
  Register #(.width(3)) register_20 (.D(RegWriteAdrM), .Q(out_23), .clk(clock_21_out));  // open: en, clr
  Register #(.width(1)) register_21 (.D(register_15_q), .Q(Mem_to_Reg), .clk(clock_22_out));  // open: en, clr
  Register #(.width(16)) register_22 (.D(ALUOutM), .Q(register_22_q), .clk(clock_23_out));  // open: en, clr
  assign out_7 = Add_ADD ? 1'b0 : 1'bz;  // Controlled_Buffer controlled_buffer_81
  assign out_3 = Add_ADD ? 1'b1 : 1'bz;  // Controlled_Buffer controlled_buffer_82
  assign out_7 = Add_SUB ? 1'b0 : 1'bz;  // Controlled_Buffer controlled_buffer_83
  assign out_3 = Add_SUB ? 1'b1 : 1'bz;  // Controlled_Buffer controlled_buffer_84
  assign out_7 = Shift_OP ? 1'b0 : 1'bz;  // Controlled_Buffer controlled_buffer_85
  assign out_3 = Shift_OP ? 1'b1 : 1'bz;  // Controlled_Buffer controlled_buffer_86
  Multiplexer #(.width(16), .disabled(0), .enable("false")) multiplexer_7 (
    .in0(register_22_q), .in1(IO_Data_Out), .out(out_22), .sel(Mem_to_Reg));
  assign out_16 = Add_ADD ? 1'b0 : 1'bz;  // Controlled_Buffer controlled_buffer_87
  assign out_17 = Add_ADD ? 4'b0000 : 4'bz;  // Controlled_Buffer controlled_buffer_88
  assign out_16 = Add_SUB ? 1'b0 : 1'bz;  // Controlled_Buffer controlled_buffer_89
  assign out_17 = Add_SUB ? 4'b0000 : 4'bz;  // Controlled_Buffer controlled_buffer_90
  assign out_16 = Shift_OP ? 1'b0 : 1'bz;  // Controlled_Buffer controlled_buffer_91
  assign out_17 = Shift_OP ? 4'b0000 : 4'bz;  // Controlled_Buffer controlled_buffer_92
  assign out_13 = Move_Imm_MOV ? 3'b000 : 3'bz;  // Controlled_Buffer controlled_buffer_93
  assign out_15 = Move_Imm_MOV ? 3'b000 : 3'bz;  // Controlled_Buffer controlled_buffer_94
  assign out_13 = Move_Imm_CMP ? IR[10:8] : 3'bz;  // Controlled_Buffer controlled_buffer_95
  assign out_15 = Move_Imm_CMP ? 3'b000 : 3'bz;  // Controlled_Buffer controlled_buffer_96
  assign out_13 = Move_Imm_ADD ? IR[10:8] : 3'bz;  // Controlled_Buffer controlled_buffer_97
  assign out_15 = Move_Imm_ADD ? 3'b000 : 3'bz;  // Controlled_Buffer controlled_buffer_98
  assign out_13 = Move_Imm_SUB ? IR[10:8] : 3'bz;  // Controlled_Buffer controlled_buffer_99
  assign out_15 = Move_Imm_SUB ? 3'b000 : 3'bz;  // Controlled_Buffer controlled_buffer_100
  assign out_13 = Move_Long_OP ? 3'b000 : 3'bz;  // Controlled_Buffer controlled_buffer_101
  assign out_15 = Move_Long_OP ? 3'b000 : 3'bz;  // Controlled_Buffer controlled_buffer_102
  Demultiplexer #(.select(2), .disabled(0), .enable("false")) demultiplexer_1 (
    .out0(demultiplexer_1_out0), .out2(demultiplexer_1_out2), .in(Mem_Write), .sel(IO_Selection));  // open: out1, out3
  Comparator #(.width(12)) comparator_1 (.a(ALUOutM[11:0]), .b(12'hff0), .eq(comparator_1_eq));  // open: gt, lt
  Comparator #(.width(12)) comparator_2 (.a(ALUOutM[11:0]), .b(12'hff1), .eq(comparator_2_eq));  // open: gt, lt
  Comparator #(.width(12)) comparator_3 (.a(ALUOutM[11:0]), .b(12'hff2), .eq(comparator_3_eq));  // open: gt, lt
  Decoder #(.select(3), .disabled(0), .enable("false")) decoder_3 (
    .out0(decoder_3_out0), .out1(Add_OP), .out2(Move_Imm_OP), .out3(ALU_OP), .out4(LD_ST_Reg_OP),
    .out5(LD_ST_Imm_OP), .out6(Cond_Branch_OP), .out7(decoder_3_out7), .sel(IR[15:13]));
  assign out_11 = Move_Imm_MOV ? 1'b1 : 1'bz;  // Controlled_Buffer controlled_buffer_103
  assign out_12 = Move_Imm_MOV ? {{8{1'b0}}, IR[7:0]} : 16'bz;  // Controlled_Buffer controlled_buffer_104
  assign out_11 = Move_Imm_CMP ? 1'b1 : 1'bz;  // Controlled_Buffer controlled_buffer_105
  assign out_12 = Move_Imm_CMP ? {{8{1'b0}}, IR[7:0]} : 16'bz;  // Controlled_Buffer controlled_buffer_106
  assign out_11 = Move_Imm_ADD ? 1'b1 : 1'bz;  // Controlled_Buffer controlled_buffer_107
  assign out_12 = Move_Imm_ADD ? {{8{1'b0}}, IR[7:0]} : 16'bz;  // Controlled_Buffer controlled_buffer_108
  assign out_11 = Move_Imm_SUB ? 1'b1 : 1'bz;  // Controlled_Buffer controlled_buffer_109
  assign out_12 = Move_Imm_SUB ? {{8{1'b0}}, IR[7:0]} : 16'bz;  // Controlled_Buffer controlled_buffer_110
  assign out_11 = Move_Long_OP ? 1'b1 : 1'bz;  // Controlled_Buffer controlled_buffer_111
  assign out_12 = Move_Long_OP ? {4'b0000, IR[11:0]} : 16'bz;  // Controlled_Buffer controlled_buffer_112
  RAM #(.addrWidth(12), .dataWidth(16), .bus("separate")) ram_1 (
    .addr(ALUOutM[11:0]), .din(IO_Data_In), .data(ram_1_data), .str(demultiplexer_1_out0), .clk(clock_24_out));  // open: sel, ld, clr
  Clock clock_24 (.out(clock_24_out));
  assign controlled_buffer_113_out = nor_1_out ? 2'b00 : 2'bz;  // Controlled_Buffer controlled_buffer_113
  nor nor_1 (nor_1_out, comparator_3_eq, comparator_2_eq, comparator_1_eq);
  assign controlled_buffer_113_out = comparator_1_eq ? 2'b01 : 2'bz;  // Controlled_Buffer controlled_buffer_114
  assign controlled_buffer_113_out = comparator_2_eq ? 2'b10 : 2'bz;  // Controlled_Buffer controlled_buffer_115
  assign controlled_buffer_113_out = comparator_3_eq ? 2'b11 : 2'bz;  // Controlled_Buffer controlled_buffer_116
  Decoder #(.disabled(0)) decoder_4 (.out0(Inherent_OP), .out1(Shift_OP), .sel(IR[12]), .en(decoder_3_out0));
  Decoder #(.disabled(0)) decoder_5 (.out0(decoder_5_out0), .out1(Move_Long_OP), .sel(IR[12]), .en(decoder_3_out7));
  Decoder #(.select(2), .disabled(0)) decoder_6 (
    .out0(Move_Imm_MOV), .out1(Move_Imm_CMP), .out2(Move_Imm_ADD), .out3(Move_Imm_SUB), .sel(IR[12:11]),
    .en(Move_Imm_OP));
  Register #(.width(16)) register_23 (.D(ram_1_data), .Q(register_23_q), .clk(clock_25_out));  // open: en, clr
  Clock clock_25 (.out(clock_25_out));
  Register #(.width(16)) register_24 (.D(Processor_Data_In), .Q(register_24_q), .clk(clock_26_out));  // open: en, clr
  Clock clock_26 (.out(clock_26_out));
  Register #(.width(16)) register_25 (
    .D(IO_Data_In), .en(demultiplexer_1_out2), .Q(out_26), .clk(clock_27_out));  // open: clr
  Clock clock_27 (.out(clock_27_out));
  Clock clock_28 (.out(clock_28_out));
  Keyboard keyboard_1 (.clk(clock_28_out), .avail(keyboard_1_avail[8]), .data(keyboard_1_data));  // open: re, clr
  Register #(.width(2)) register_26 (
    .D(controlled_buffer_113_out), .Q(IO_Selection), .clk(clock_29_out));  // open: en, clr
  Clock clock_29 (.out(clock_29_out));
  assign out_9 = Move_Imm_MOV ? 1'b0 : 1'bz;  // Controlled_Buffer controlled_buffer_117
  assign out_10 = Move_Imm_MOV ? 8'hcf : 8'bz;  // Controlled_Buffer controlled_buffer_118
  assign out_9 = Move_Imm_CMP ? 1'b0 : 1'bz;  // Controlled_Buffer controlled_buffer_119
  assign out_10 = Move_Imm_CMP ? 8'hf8 : 8'bz;  // Controlled_Buffer controlled_buffer_120
  assign out_9 = Move_Imm_ADD ? 1'b0 : 1'bz;  // Controlled_Buffer controlled_buffer_121
  assign out_10 = Move_Imm_ADD ? 8'hf7 : 8'bz;  // Controlled_Buffer controlled_buffer_122
  assign out_9 = Move_Imm_SUB ? 1'b0 : 1'bz;  // Controlled_Buffer controlled_buffer_123
  assign out_10 = Move_Imm_SUB ? 8'hf8 : 8'bz;  // Controlled_Buffer controlled_buffer_124
  assign out_9 = Move_Long_OP ? 1'b0 : 1'bz;  // Controlled_Buffer controlled_buffer_125
  assign out_10 = Move_Long_OP ? 8'hf : 8'bz;  // Controlled_Buffer controlled_buffer_126
  Decoder #(.disabled(0)) decoder_7 (
    .out0(Uncond_Branch_OP), .out1(Branch_Subroutine_OP), .sel(IR[11]), .en(decoder_5_out0));
  assign out_6 = Move_Imm_MOV ? IR[10:8] : 3'bz;  // Controlled_Buffer controlled_buffer_127
  assign out_6 = Move_Imm_CMP ? 3'b000 : 3'bz;  // Controlled_Buffer controlled_buffer_128
  assign out_6 = Move_Imm_ADD ? IR[10:8] : 3'bz;  // Controlled_Buffer controlled_buffer_129
  assign out_6 = Move_Imm_SUB ? IR[10:8] : 3'bz;  // Controlled_Buffer controlled_buffer_130
  assign out_6 = Move_Long_OP ? 3'b000 : 3'bz;  // Controlled_Buffer controlled_buffer_131
  assign out_7 = Move_Imm_MOV ? 1'b0 : 1'bz;  // Controlled_Buffer controlled_buffer_132
  assign out_3 = Move_Imm_MOV ? 1'b1 : 1'bz;  // Controlled_Buffer controlled_buffer_133
  assign out_7 = Move_Imm_CMP ? 1'b0 : 1'bz;  // Controlled_Buffer controlled_buffer_134
  assign out_3 = Move_Imm_CMP ? 1'b0 : 1'bz;  // Controlled_Buffer controlled_buffer_135
  assign out_7 = Move_Imm_ADD ? 1'b0 : 1'bz;  // Controlled_Buffer controlled_buffer_136
  assign out_3 = Move_Imm_ADD ? 1'b1 : 1'bz;  // Controlled_Buffer controlled_buffer_137
  assign out_7 = Move_Imm_SUB ? 1'b0 : 1'bz;  // Controlled_Buffer controlled_buffer_138
  assign out_3 = Move_Imm_SUB ? 1'b1 : 1'bz;  // Controlled_Buffer controlled_buffer_139
  assign out_7 = Move_Long_OP ? 1'b0 : 1'bz;  // Controlled_Buffer controlled_buffer_140
  assign out_3 = Move_Long_OP ? 1'b1 : 1'bz;  // Controlled_Buffer controlled_buffer_141
  Multiplexer #(.select(2), .width(16), .disabled(0), .enable("false")) multiplexer_8 (
    .in0(register_23_q), .in1(register_24_q), .in2(out_26),
    .in3({{7{1'b0}}, keyboard_1_avail[8], 1'b0, keyboard_1_data}), .out(IO_Data_Out), .sel(IO_Selection));
  xor xor_1 (xor_1_out, N, V);
  and and_1 (and_1_out, Z, xor_1_out);
  assign out_16 = Move_Imm_MOV ? 1'b0 : 1'bz;  // Controlled_Buffer controlled_buffer_142
  assign out_17 = Move_Imm_MOV ? 4'b0000 : 4'bz;  // Controlled_Buffer controlled_buffer_143
  assign out_16 = Move_Imm_CMP ? 1'b0 : 1'bz;  // Controlled_Buffer controlled_buffer_144
  assign out_17 = Move_Imm_CMP ? 4'b0000 : 4'bz;  // Controlled_Buffer controlled_buffer_145
  assign out_16 = Move_Imm_ADD ? 1'b0 : 1'bz;  // Controlled_Buffer controlled_buffer_146
  assign out_17 = Move_Imm_ADD ? 4'b0000 : 4'bz;  // Controlled_Buffer controlled_buffer_147
  assign out_16 = Move_Imm_SUB ? 1'b0 : 1'bz;  // Controlled_Buffer controlled_buffer_148
  assign out_17 = Move_Imm_SUB ? 4'b0000 : 4'bz;  // Controlled_Buffer controlled_buffer_149
  assign out_16 = Move_Long_OP ? 1'b0 : 1'bz;  // Controlled_Buffer controlled_buffer_150
  assign out_17 = Move_Long_OP ? 4'b0000 : 4'bz;  // Controlled_Buffer controlled_buffer_151
  not not_3 (not_3_out, Z);
  not not_4 (not_4_out, N);
  and and_2 (and_2_out, N, not_3_out, V);
  and and_3 (and_3_out, not_4_out, not_3_out, not_5_out);
  or or_1 (or_1_out, and_2_out, and_3_out);
  not not_5 (not_5_out, V);
  xor xor_2 (xor_2_out, N, V);
  or or_2 (or_2_out, Z, not_6_out);
  xnor xnor_1 (xnor_1_out, N, V);
  assign out_13 = ALU_Common ? IR[5:3] : 3'bz;  // Controlled_Buffer controlled_buffer_152
  assign out_15 = ALU_Common ? IR[8:6] : 3'bz;  // Controlled_Buffer controlled_buffer_153
  assign out_13 = ALU_CMP ? IR[5:3] : 3'bz;  // Controlled_Buffer controlled_buffer_154
  assign out_15 = ALU_CMP ? IR[8:6] : 3'bz;  // Controlled_Buffer controlled_buffer_155
  assign out_13 = ALU_TST ? IR[5:3] : 3'bz;  // Controlled_Buffer controlled_buffer_156
  assign out_15 = ALU_TST ? IR[8:6] : 3'bz;  // Controlled_Buffer controlled_buffer_157
  not not_6 (not_6_out, C);
  not not_7 (not_7_out, Z);
  and and_4 (and_4_out, not_7_out, C);
  and and_5 (PC_Source, out_16, Branch_Taken);
  not not_8 (not_8_out, V);
  not not_9 (not_9_out, N);
  assign out_11 = ALU_Common ? 1'b0 : 1'bz;  // Controlled_Buffer controlled_buffer_158
  assign out_12 = ALU_Common ? {16{1'b0}} : 16'bz;  // Controlled_Buffer controlled_buffer_159
  assign out_11 = ALU_CMP ? 1'b0 : 1'bz;  // Controlled_Buffer controlled_buffer_160
  assign out_12 = ALU_CMP ? {16{1'b0}} : 16'bz;  // Controlled_Buffer controlled_buffer_161
  assign out_11 = ALU_TST ? 1'b0 : 1'bz;  // Controlled_Buffer controlled_buffer_162
  assign out_12 = ALU_TST ? {16{1'b0}} : 16'bz;  // Controlled_Buffer controlled_buffer_163
  not not_10 (not_10_out, C);
  Comparator #(.width(3)) comparator_4 (.a(RegWriteAdrM), .b(RegReadAdr1E), .eq(comparator_4_eq));  // open: gt, lt
  Comparator #(.width(3)) comparator_5 (.a(out_23), .b(RegReadAdr1E), .eq(comparator_5_eq));  // open: gt, lt
  not not_11 (not_11_out, Z);
  Multiplexer #(.select(4), .width(8), .disabled(0), .enable("false")) multiplexer_9 (
    .in0(8'hc0), .in1(8'hc1), .in2(8'hc2), .in3(8'he3), .in4(8'he4), .in5(8'he5), .in6(8'he6), .in7(8'hf7),
    .in8(8'hf8), .in9(8'hc9), .in10(8'hca), .out(multiplexer_9_out), .sel(IR[12:9]));  // open: in11, in12, in13, in14, in15
  assign out_10 = ALU_Common ? multiplexer_9_out : 8'bz;  // Controlled_Buffer controlled_buffer_164
  assign out_9 = ALU_Common ? 1'b0 : 1'bz;  // Controlled_Buffer controlled_buffer_165
  and and_6 (and_6_out[0], RegWriteM, comparator_4_eq);
  and and_7 (and_6_out[1], out_24, comparator_5_eq);
  Multiplexer #(.select(4), .disabled(0), .enable("false")) multiplexer_10 (
    .in0(Z), .in1(not_11_out), .in2(C), .in3(not_10_out), .in4(N), .in5(not_9_out), .in6(V), .in7(not_8_out),
    .in8(and_4_out), .in9(or_2_out), .in10(xnor_1_out), .in11(xor_2_out), .in12(or_1_out), .in13(and_1_out),
    .in15(1'b1), .out(Branch_Taken), .sel(out_17));  // open: in14
  assign out_9 = ALU_CMP ? 1'b0 : 1'bz;  // Controlled_Buffer controlled_buffer_166
  assign out_10 = ALU_CMP ? 8'hf8 : 8'bz;  // Controlled_Buffer controlled_buffer_167
  assign out_9 = ALU_TST ? 1'b0 : 1'bz;  // Controlled_Buffer controlled_buffer_168
  assign out_10 = ALU_TST ? 8'hf0 : 8'bz;  // Controlled_Buffer controlled_buffer_169
  Multiplexer #(.select(2), .width(2), .disabled(0), .enable("false")) multiplexer_11 (
    .in0(2'b00), .in1(2'b01), .in2(2'b10), .in3(2'b01), .out(out_5), .sel(and_6_out));
  Decoder #(.select(4), .disabled(0)) decoder_8 (
    .out0(decoder_8_out0), .out1(decoder_8_out1), .out2(decoder_8_out2), .out3(decoder_8_out3),
    .out4(decoder_8_out4), .out5(decoder_8_out5), .out6(decoder_8_out6), .out7(decoder_8_out7),
    .out8(decoder_8_out8), .out9(decoder_8_out9), .out10(decoder_8_out10), .out11(ALU_CMP), .out12(ALU_TST),
    .sel(IR[12:9]), .en(ALU_OP));  // open: out13, out14, out15
  assign out_7 = ALU_Common ? 1'b0 : 1'bz;  // Controlled_Buffer controlled_buffer_170
  assign out_6 = ALU_Common ? IR[2:0] : 3'bz;  // Controlled_Buffer controlled_buffer_171
  assign out_3 = ALU_Common ? 1'b1 : 1'bz;  // Controlled_Buffer controlled_buffer_172
  assign out_7 = ALU_CMP ? 1'b0 : 1'bz;  // Controlled_Buffer controlled_buffer_173
  assign out_6 = ALU_CMP ? 3'b000 : 3'bz;  // Controlled_Buffer controlled_buffer_174
  assign out_3 = ALU_CMP ? 1'b0 : 1'bz;  // Controlled_Buffer controlled_buffer_175
  assign out_7 = ALU_TST ? 1'b0 : 1'bz;  // Controlled_Buffer controlled_buffer_176
  assign out_6 = ALU_TST ? 3'b000 : 3'bz;  // Controlled_Buffer controlled_buffer_177
  assign out_3 = ALU_TST ? 1'b0 : 1'bz;  // Controlled_Buffer controlled_buffer_178
  Comparator #(.width(3)) comparator_6 (.a(RegWriteAdrM), .b(RegReadAdr2E), .eq(comparator_6_eq));  // open: gt, lt
  Comparator #(.width(3)) comparator_7 (.a(out_23), .b(RegReadAdr2E), .eq(comparator_7_eq));  // open: gt, lt
  or or_3 (ALU_Common, decoder_8_out0, decoder_8_out1, decoder_8_out2, decoder_8_out3, decoder_8_out4, decoder_8_out5, decoder_8_out6, decoder_8_out7, decoder_8_out8, decoder_8_out9, decoder_8_out10);
  assign out_16 = ALU_Common ? 1'b0 : 1'bz;  // Controlled_Buffer controlled_buffer_179
  assign out_17 = ALU_Common ? 4'b0000 : 4'bz;  // Controlled_Buffer controlled_buffer_180
  assign out_16 = ALU_CMP ? 1'b0 : 1'bz;  // Controlled_Buffer controlled_buffer_181
  assign out_17 = ALU_CMP ? 4'b0000 : 4'bz;  // Controlled_Buffer controlled_buffer_182
  assign out_16 = ALU_TST ? 1'b0 : 1'bz;  // Controlled_Buffer controlled_buffer_183
  assign out_17 = ALU_TST ? 4'b0000 : 4'bz;  // Controlled_Buffer controlled_buffer_184
  and and_8 (and_8_out[0], RegWriteM, comparator_6_eq);
  and and_9 (and_8_out[1], out_24, comparator_7_eq);
  Multiplexer #(.select(2), .width(2), .disabled(0), .enable("false")) multiplexer_12 (
    .in0(2'b00), .in1(2'b01), .in2(2'b10), .in3(2'b01), .out(out_4), .sel(and_8_out));
  Register #(.width(1)) register_27 (
    .D(out_14), .Q(register_27_q), .clk(clock_30_out), .clr(register_29_q));  // open: en
  Clock clock_30 (.out(clock_30_out));
  not not_12 (not_12_out, out_16);
  Register #(.width(1)) register_28 (.D(in_2), .Q(register_28_q), .clk(clock_31_out));  // open: en, clr
  Clock clock_31 (.out(clock_31_out));
  and and_10 (and_10_out, register_27_q, not_12_out, register_28_q);
  assign ISRAdr = and_10_out ? 12'h1 : 12'bz;  // Controlled_Buffer controlled_buffer_185
  Register #(.width(1)) register_29 (
    .D(and_10_out), .Q(register_29_q), .clk(clock_32_out), .clr(buffer_1_out));  // open: en
  buf buffer_1 (buffer_1_out, clock_32_out);
  Clock clock_32 (.out(clock_32_out));
  assign FlushDWillCome = and_10_out ? 1'b1 : 1'bz;  // Controlled_Buffer controlled_buffer_186
  assign BranchISR = and_10_out ? 1'b1 : 1'bz;  // Controlled_Buffer controlled_buffer_187
  assign out_13 = LD_ST_Reg_LD ? IR[5:3] : 3'bz;  // Controlled_Buffer controlled_buffer_188
  assign out_15 = LD_ST_Reg_LD ? IR[8:6] : 3'bz;  // Controlled_Buffer controlled_buffer_189
  assign out_13 = LD_ST_Imm_LD ? IR[5:3] : 3'bz;  // Controlled_Buffer controlled_buffer_190
  assign out_15 = LD_ST_Imm_LD ? 3'b000 : 3'bz;  // Controlled_Buffer controlled_buffer_191
  assign out_13 = LD_ST_Imm_STR ? IR[5:3] : 3'bz;  // Controlled_Buffer controlled_buffer_192
  assign out_15 = LD_ST_Imm_STR ? IR[2:0] : 3'bz;  // Controlled_Buffer controlled_buffer_193
  Register #(.width(12)) RetrunAdr (.D(PC), .en(and_10_out), .Q(RetrunAdr_q), .clk(clock_33_out));  // open: clr
  Clock clock_33 (.out(clock_33_out));
  assign out_11 = LD_ST_Reg_LD ? 1'b0 : 1'bz;  // Controlled_Buffer controlled_buffer_194
  assign out_12 = LD_ST_Reg_LD ? {16{1'b0}} : 16'bz;  // Controlled_Buffer controlled_buffer_195
  assign out_11 = LD_ST_Imm_LD ? 1'b1 : 1'bz;  // Controlled_Buffer controlled_buffer_196
  assign out_12 = LD_ST_Imm_LD ? {{10{1'b0}}, IR[11:6]} : 16'bz;  // Controlled_Buffer controlled_buffer_197
  assign out_11 = LD_ST_Imm_STR ? 1'b1 : 1'bz;  // Controlled_Buffer controlled_buffer_198
  assign out_12 = LD_ST_Imm_STR ? {{10{1'b0}}, IR[11:6]} : 16'bz;  // Controlled_Buffer controlled_buffer_199
  Pull_Resistor pull_resistor_2 (.node(RTI));
  assign BranchISR = RTI ? 1'b1 : 1'bz;  // Controlled_Buffer controlled_buffer_200
  assign ISRAdr = RTI ? RetrunAdr_q : 12'bz;  // Controlled_Buffer controlled_buffer_201
  Comparator #(.width(3)) comparator_8 (.a(RegWriteAdrE), .b(out_13), .eq(comparator_8_eq));  // open: gt, lt
  Comparator #(.width(3)) comparator_9 (.a(RegWriteAdrE), .b(out_15), .eq(comparator_9_eq));  // open: gt, lt
  assign FlushDWillCome = PC_Source ? 1'b1 : 1'bz;  // Controlled_Buffer controlled_buffer_202
  Pull_Resistor pull_resistor_3 (.node(FlushDWillCome));
  Decoder #(.disabled(0)) decoder_9 (.out0(LD_ST_Reg_LD), .sel(IR[9]), .en(LD_ST_Reg_OP));  // open: out1
  assign out_9 = LD_ST_Reg_LD ? 1'b0 : 1'bz;  // Controlled_Buffer controlled_buffer_203
  assign out_10 = LD_ST_Reg_LD ? 8'h7 : 8'bz;  // Controlled_Buffer controlled_buffer_204
  Decoder #(.disabled(0)) decoder_10 (.out0(LD_ST_Imm_LD), .out1(LD_ST_Imm_STR), .sel(IR[12]), .en(LD_ST_Imm_OP));
  or or_4 (or_4_out, comparator_8_eq, comparator_9_eq);
  Register #(.width(1)) register_30 (
    .D(FlushDWillCome), .Q(FlushD), .clk(clock_34_out), .clr(buffer_2_out));  // open: en
  buf buffer_2 (buffer_2_out, clock_34_out);
  Clock clock_34 (.out(clock_34_out));
  assign out_9 = LD_ST_Imm_LD ? 1'b0 : 1'bz;  // Controlled_Buffer controlled_buffer_205
  assign out_10 = LD_ST_Imm_LD ? 8'h7 : 8'bz;  // Controlled_Buffer controlled_buffer_206
  assign out_9 = LD_ST_Imm_STR ? 1'b1 : 1'bz;  // Controlled_Buffer controlled_buffer_207
  assign out_10 = LD_ST_Imm_STR ? 8'h7 : 8'bz;  // Controlled_Buffer controlled_buffer_208
  and and_11 (StallD, MemToRegE, or_4_out);
  Clock clock_35 (.out(clock_35_out));
  assign out_6 = LD_ST_Reg_LD ? IR[2:0] : 3'bz;  // Controlled_Buffer controlled_buffer_209
  Register #(.width(1)) register_31 (.D(StallD), .Q(FlushE), .clk(clock_35_out), .clr(buffer_3_out));  // open: en
  buf buffer_3 (buffer_3_out, clock_35_out);
  assign out_7 = LD_ST_Reg_LD ? 1'b1 : 1'bz;  // Controlled_Buffer controlled_buffer_210
  assign out_3 = LD_ST_Reg_LD ? 1'b1 : 1'bz;  // Controlled_Buffer controlled_buffer_211
  assign out_7 = LD_ST_Imm_LD ? 1'b1 : 1'bz;  // Controlled_Buffer controlled_buffer_212
  assign out_6 = LD_ST_Imm_LD ? IR[2:0] : 3'bz;  // Controlled_Buffer controlled_buffer_213
  assign out_3 = LD_ST_Imm_LD ? 1'b1 : 1'bz;  // Controlled_Buffer controlled_buffer_214
  assign out_7 = LD_ST_Imm_STR ? 1'b0 : 1'bz;  // Controlled_Buffer controlled_buffer_215
  assign out_6 = LD_ST_Imm_STR ? 3'b000 : 3'bz;  // Controlled_Buffer controlled_buffer_216
  assign out_3 = LD_ST_Imm_STR ? 1'b0 : 1'bz;  // Controlled_Buffer controlled_buffer_217
  Adder #(.width(3)) adder_2 (.a(Stack_Pointer_q), .b(3'b001), .out(adder_2_out));  // open: cin, cout
  Subtractor #(.width(3)) subtractor_2 (.a(Stack_Pointer_q), .b(3'b001), .out(subtractor_2_out));  // open: bin, bout
  assign controlled_buffer_218_out = Branch_Subroutine_OP ? 1'b0 : 1'bz;  // Controlled_Buffer controlled_buffer_218
  assign controlled_buffer_218_out = Inherent_RTS ? 1'b1 : 1'bz;  // Controlled_Buffer controlled_buffer_219
  assign out_16 = LD_ST_Reg_LD ? 1'b0 : 1'bz;  // Controlled_Buffer controlled_buffer_220
  assign out_17 = LD_ST_Reg_LD ? 4'b0000 : 4'bz;  // Controlled_Buffer controlled_buffer_221
  assign out_16 = LD_ST_Imm_LD ? 1'b0 : 1'bz;  // Controlled_Buffer controlled_buffer_222
  assign out_17 = LD_ST_Imm_LD ? 4'b0000 : 4'bz;  // Controlled_Buffer controlled_buffer_223
  assign out_16 = LD_ST_Imm_STR ? 1'b0 : 1'bz;  // Controlled_Buffer controlled_buffer_224
  assign out_17 = LD_ST_Imm_STR ? 4'b0000 : 4'bz;  // Controlled_Buffer controlled_buffer_225
  Multiplexer #(.width(3), .disabled(0), .enable("false")) multiplexer_13 (
    .in0(adder_2_out), .in1(subtractor_2_out), .out(multiplexer_13_out), .sel(controlled_buffer_218_out));
  Register #(.width(3)) Stack_Pointer (
    .D(multiplexer_13_out), .en(or_5_out), .Q(Stack_Pointer_q), .clk(clock_36_out));  // open: clr
  Clock clock_36 (.out(clock_36_out));
  or or_5 (or_5_out, Branch_Subroutine_OP, Inherent_RTS);
  Decoder #(.select(3), .disabled(0)) decoder_11 (
    .out0(decoder_11_out0), .out1(decoder_11_out1), .out2(decoder_11_out2), .out3(decoder_11_out3),
    .out4(decoder_11_out4), .out5(decoder_11_out5), .out6(decoder_11_out6), .out7(decoder_11_out7),
    .sel(Stack_Pointer_q), .en(Branch_Subroutine_OP));
  Clock clock_37 (.out(clock_37_out));
  assign out_13 = Cond_Branch_OP ? 3'b000 : 3'bz;  // Controlled_Buffer controlled_buffer_226
  assign out_15 = Cond_Branch_OP ? 3'b000 : 3'bz;  // Controlled_Buffer controlled_buffer_227
  assign out_13 = Uncond_Branch_OP ? 3'b000 : 3'bz;  // Controlled_Buffer controlled_buffer_228
  assign out_15 = Uncond_Branch_OP ? 3'b000 : 3'bz;  // Controlled_Buffer controlled_buffer_229
  assign out_13 = Branch_Subroutine_OP ? 3'b000 : 3'bz;  // Controlled_Buffer controlled_buffer_230
  assign out_15 = Branch_Subroutine_OP ? 3'b000 : 3'bz;  // Controlled_Buffer controlled_buffer_231
  Register #(.width(12)) r0 (.D(PC), .en(decoder_11_out0), .Q(r0_q), .clk(clock_37_out));  // open: clr
  Register #(.width(12)) r1 (.D(PC), .en(decoder_11_out1), .Q(r1_q), .clk(clock_37_out));  // open: clr
  Register #(.width(12)) r2 (.D(PC), .en(decoder_11_out2), .Q(r2_q), .clk(clock_37_out));  // open: clr
  Register #(.width(12)) r3 (.D(PC), .en(decoder_11_out3), .Q(r3_q), .clk(clock_37_out));  // open: clr
  Register #(.width(12)) r4 (.D(PC), .en(decoder_11_out4), .Q(r4_q), .clk(clock_37_out));  // open: clr
  Register #(.width(12)) r5 (.D(PC), .en(decoder_11_out5), .Q(r5_q), .clk(clock_37_out));  // open: clr
  Register #(.width(12)) r6 (.D(PC), .en(decoder_11_out6), .Q(r6_q), .clk(clock_37_out));  // open: clr
  Register #(.width(12)) r7 (.D(PC), .en(decoder_11_out7), .Q(r7_q), .clk(clock_37_out));  // open: clr
  Subtractor #(.width(3)) subtractor_3 (.a(Stack_Pointer_q), .b(3'b001), .out(subtractor_3_out));  // open: bin, bout
  Multiplexer #(.width(3), .disabled(0), .enable("false")) multiplexer_14 (
    .in0(3'b000), .in1(3'b111), .out(multiplexer_14_out), .sel(IR[8]));
  Multiplexer #(.disabled(0), .enable("false")) multiplexer_15 (
    .in0(1'b0), .in1(1'b1), .out(multiplexer_15_out[11]), .sel(IR[8]));
  Multiplexer #(.disabled(0), .enable("false")) multiplexer_16 (
    .in0(1'b0), .in1(1'b1), .out(multiplexer_16_out[11]), .sel(IR[8]));
  Multiplexer #(.select(3), .width(12), .enable("false")) multiplexer_17 (
    .in0(r0_q), .in1(r1_q), .in2(r2_q), .in3(r3_q), .in4(r4_q), .in5(r5_q), .in6(r6_q), .in7(r7_q),
    .out(RTSAdr), .sel(subtractor_3_out));
  assign out_11 = Cond_Branch_OP ? 1'b1 : 1'bz;  // Controlled_Buffer controlled_buffer_232
  assign out_12 = Cond_Branch_OP ? {4'b0000, multiplexer_14_out, IR[8:0]} : 16'bz;  // Controlled_Buffer controlled_buffer_233
  assign out_11 = Uncond_Branch_OP ? 1'b1 : 1'bz;  // Controlled_Buffer controlled_buffer_234
  assign out_11 = Branch_Subroutine_OP ? 1'b1 : 1'bz;  // Controlled_Buffer controlled_buffer_235
  assign out_12 = Branch_Subroutine_OP ? {4'b0000, multiplexer_16_out[11], IR[10:0]} : 16'bz;  // Controlled_Buffer controlled_buffer_236
  assign out_12 = Uncond_Branch_OP ? {4'b0000, multiplexer_15_out[11], IR[10:0]} : 16'bz;  // Controlled_Buffer controlled_buffer_237
  assign out_9 = Cond_Branch_OP ? 1'b0 : 1'bz;  // Controlled_Buffer controlled_buffer_238
  assign out_10 = Cond_Branch_OP ? 8'hf : 8'bz;  // Controlled_Buffer controlled_buffer_239
  assign out_9 = Uncond_Branch_OP ? 1'b0 : 1'bz;  // Controlled_Buffer controlled_buffer_240
  assign out_10 = Uncond_Branch_OP ? 8'hf : 8'bz;  // Controlled_Buffer controlled_buffer_241
  assign out_9 = Branch_Subroutine_OP ? 1'b0 : 1'bz;  // Controlled_Buffer controlled_buffer_242
  assign out_10 = Branch_Subroutine_OP ? 8'hf : 8'bz;  // Controlled_Buffer controlled_buffer_243
  assign out_7 = Cond_Branch_OP ? 1'b0 : 1'bz;  // Controlled_Buffer controlled_buffer_244
  assign out_6 = Cond_Branch_OP ? 3'b000 : 3'bz;  // Controlled_Buffer controlled_buffer_245
  assign out_3 = Cond_Branch_OP ? 1'b0 : 1'bz;  // Controlled_Buffer controlled_buffer_246
  assign out_7 = Uncond_Branch_OP ? 1'b0 : 1'bz;  // Controlled_Buffer controlled_buffer_247
  assign out_6 = Uncond_Branch_OP ? 3'b000 : 3'bz;  // Controlled_Buffer controlled_buffer_248
  assign out_3 = Uncond_Branch_OP ? 1'b0 : 1'bz;  // Controlled_Buffer controlled_buffer_249
  assign out_7 = Branch_Subroutine_OP ? 1'b0 : 1'bz;  // Controlled_Buffer controlled_buffer_250
  assign out_6 = Branch_Subroutine_OP ? 3'b000 : 3'bz;  // Controlled_Buffer controlled_buffer_251
  assign out_3 = Branch_Subroutine_OP ? 1'b0 : 1'bz;  // Controlled_Buffer controlled_buffer_252
  Multiplexer #(.select(4), .width(4), .disabled(0), .enable("false")) multiplexer_18 (
    .in0(4'b0000), .in1(4'b0001), .in2(4'b0010), .in3(4'b0011), .in4(4'b0100), .in5(4'b0101), .in6(4'b0110),
    .in7(4'b0111), .in8(4'b1000), .in9(4'b1001), .in10(4'b1010), .in11(4'b1011), .in12(4'b1100),
    .in13(4'b1101), .out(multiplexer_18_out), .sel(IR[12:9]));  // open: in14, in15
  assign out_17 = Cond_Branch_OP ? multiplexer_18_out : 4'bz;  // Controlled_Buffer controlled_buffer_253
  assign out_16 = Cond_Branch_OP ? 1'b1 : 1'bz;  // Controlled_Buffer controlled_buffer_254
  assign out_16 = Uncond_Branch_OP ? 1'b1 : 1'bz;  // Controlled_Buffer controlled_buffer_255
  assign out_17 = Uncond_Branch_OP ? 4'b1111 : 4'bz;  // Controlled_Buffer controlled_buffer_256
  assign out_16 = Branch_Subroutine_OP ? 1'b1 : 1'bz;  // Controlled_Buffer controlled_buffer_257
  assign out_17 = Branch_Subroutine_OP ? 4'b1111 : 4'bz;  // Controlled_Buffer controlled_buffer_258

  assign out_18 = in_2;
  assign out_19 = out_13;
  assign out_21 = out_15;
  assign Processor_Data_Out = out_26;

  // Other names for the same wires on the sheet: ALU_Con[7:0] = out_25; ALUConD[7:0] = out_10;
  //   IO_Address[11:0] = ALUOutM[11:0]; ALUSource2D = out_11; Branch_Condition[3:0] = out_17;
  //   BranchConditionD[3:0] = out_17; BranchD = out_16; Forward1E[1:0] = out_5; Forward2E[1:0] = out_4; IEN = out_14;
  //   IRQ = in_2; MemtoRegD = out_7; MemToRegW = Mem_to_Reg; MemWriteD = out_9; MemWriteM = Mem_Write;
  //   Offset_Register[15:0] = out_12; OffsetRegisterD[15:0] = out_12; PC_Offset[11:0] = out_12[11:0];
  //   Processor_Data_Output[15:0] = out_26; Reg_Read_Adr1[2:0] = out_13; RegReadAdr1D[2:0] = out_13;
  //   Reg_Read_Adr2[2:0] = out_15; RegReadAdr2D[2:0] = out_15; RegWriteAdrD[2:0] = out_6; Reg_Write_Adr[2:0] = out_23;
  //   RegWriteAdrW[2:0] = out_23; RegWriteD = out_3; Reg_Write = out_24; RegWriteW = out_24; ResultW[15:0] = out_22;
  //   StallF = StallD; SubroutineCall = Branch_Subroutine_OP; SubroutineReturn = Inherent_RTS

  // Notes on the sheet:
  //   Fetch
  //   contents of rom_1 (hex, n*v repeats v):
  //   e00f e00e 14*0 4204 4303 1c5b 3052 c3fd 2049 fff1 b003 e7ff
  //   Inherent
  //   Decode
  //   Execute
  //   Memory
  //   Add/Subtract Register Immediate
  //   Shift
  //   Write Back
  //   IO Memory
  //   Move/Compare/Add/Subtract Immediate
  //   Move Long
  //   Decode Unit
  //   Branch
  //   Branch Condition Logic
  //   ALU
  //   Forward
  //   Hazard Unit
  //   Handle Interrupt
  //   Interrupt
  //   Return From Interrupt
  //   Stall
  //   LD Stall
  //   Branch Stall
  //   Load/Store Register
  //   Load/Store Immediate
  //   Subroutine Stack
  //   Conditional Branch
  //   Branch to Subroutine
  //   Unconditional Branch
endmodule

module Register_File (
  input  [15:0] Data_in,
  input  [2:0] Adr1,
  input  [2:0] Adr2,
  input  Read_Write,
  input  [2:0] Data_Adr,
  output [15:0] Data_out1,
  output [15:0] Data_out2
);

  wire clock_1_out, decoder_1_out0, decoder_1_out1, decoder_1_out2, decoder_1_out3, decoder_1_out4,
       decoder_1_out5, decoder_1_out6, decoder_1_out7;
  wire [15:0] r0_q, r1_q, r2_q, r3_q, r4_q, r5_q, r6_q, r7_q;

  Decoder #(.select(3), .disabled(0)) decoder_1 (
    .out0(decoder_1_out0), .out1(decoder_1_out1), .out2(decoder_1_out2), .out3(decoder_1_out3),
    .out4(decoder_1_out4), .out5(decoder_1_out5), .out6(decoder_1_out6), .out7(decoder_1_out7),
    .sel(Data_Adr), .en(Read_Write));
  Register #(.width(16), .trigger("falling")) r0 (
    .D(Data_in), .en(decoder_1_out0), .Q(r0_q), .clk(clock_1_out));  // open: clr
  Register #(.width(16), .trigger("falling")) r1 (
    .D(Data_in), .en(decoder_1_out1), .Q(r1_q), .clk(clock_1_out));  // open: clr
  Register #(.width(16), .trigger("falling")) r2 (
    .D(Data_in), .en(decoder_1_out2), .Q(r2_q), .clk(clock_1_out));  // open: clr
  Register #(.width(16), .trigger("falling")) r3 (
    .D(Data_in), .en(decoder_1_out3), .Q(r3_q), .clk(clock_1_out));  // open: clr
  Register #(.width(16), .trigger("falling")) r4 (
    .D(Data_in), .en(decoder_1_out4), .Q(r4_q), .clk(clock_1_out));  // open: clr
  Register #(.width(16), .trigger("falling")) r5 (
    .D(Data_in), .en(decoder_1_out5), .Q(r5_q), .clk(clock_1_out));  // open: clr
  Register #(.width(16), .trigger("falling")) r6 (
    .D(Data_in), .en(decoder_1_out6), .Q(r6_q), .clk(clock_1_out));  // open: clr
  Register #(.width(16), .trigger("falling")) r7 (
    .D(Data_in), .en(decoder_1_out7), .Q(r7_q), .clk(clock_1_out));  // open: clr
  Clock clock_1 (.out(clock_1_out));
  Multiplexer #(.select(3), .width(16), .enable("false")) multiplexer_1 (
    .in0(r0_q), .in1(r1_q), .in2(r2_q), .in3(r3_q), .in4(r4_q), .in5(r5_q), .in6(r6_q), .in7(r7_q),
    .out(Data_out1), .sel(Adr1));
  Multiplexer #(.select(3), .width(16), .enable("false")) multiplexer_2 (
    .in0(r0_q), .in1(r1_q), .in2(r2_q), .in3(r3_q), .in4(r4_q), .in5(r5_q), .in6(r6_q), .in7(r7_q),
    .out(Data_out2), .sel(Adr2));
endmodule
